# Fritzing sketch Untitled Sketch (saved by Fritzing 1.0.6)
circuit board: 7.92631cm x 5.03159cm
breadboards: 1

parts:
  A1 = Wemos D32-pro
  Button_1 = Momentary Switch [package=ksa_sealed_tac_switch]
  Button_2 = Momentary Switch [package=ksa_sealed_tac_switch]
  R1 = Resistor [tolerance=±5% power=0.25W resistance=330 package=THT]
  R2 = Resistor [tolerance=±5% power=0.25W resistance=330 package=THT]
  R3 = Resistor [tolerance=±5% power=0.25W resistance=1k2 package=THT]
  Chip-detected_LED = LED - 5mm [color="Green (570nm)" current=0.030A package="5 mm [THT]"]
  Write-activity_LED = LED - 5mm [color="Green (570nm)" current=0.030A package="5 mm [THT]"]
  R4 = Resistor [tolerance=±5% power=0.25W resistance=1k2 package=THT]
  R5 = Resistor [tolerance=±5% power=0.25W resistance=3k9 package=THT]
  JP1 = Header 2 [package=jst-2-pth-kit]

nets:
  N1: A1.Pin_1, R3.Pin_0, R4.Pin_0, R5.Pin_0
  N2: A1.Pin_13, R1.Pin_1
  GND: A1.Pin_33, A1.Pin_41, A1.Pin_48, Button_1.3, Button_1.4, Button_2.1, Button_2.2, Button_2.3, Button_2.4, Chip-detected_LED.cathode, Write-activity_LED.cathode, R4.Pin_1, JP1.2
  N3: A1.Pin_37, R5.Pin_1, JP1.1
  N4: A1.Pin_42, Button_1.1, Button_1.2, R3.Pin_1
  N5: A1.Pin_47, R2.Pin_0
  N6: R1.Pin_0, Chip-detected_LED.anode
  N7: R2.Pin_1, Write-activity_LED.anode

notes:
  Probe:
  1 = inner pogo pin
  2 = two outer circle pogo pins

custom parts:
  Wemos D32-pro: A wifi&bluetooth board based ESP32-WROVER.
